// Logisim project not_gate_v1.0.circ as structural Verilog
module main (
  input  in_1,
  output out_2
);

  NOT_Gate not_gate_1 (.a(in_1), .y(out_2));
endmodule

// VHDL entity NOT_Gate, as the project stores it:
--------------------------------------------------------------------------------
-- Project :
-- File    :
-- Autor   :
-- Date    :
--
--------------------------------------------------------------------------------
-- Description :
--
--------------------------------------------------------------------------------

LIBRARY ieee;
USE ieee.std_logic_1164.all;

ENTITY NOT_Gate IS
  PORT (
    a : IN  std_logic;   -- 입력
    y : OUT std_logic    -- 출력 (a의 반전)
    );
END NOT_Gate;

ARCHITECTURE TypeArchitecture OF NOT_Gate IS
BEGIN
  y <= NOT a;
END TypeArchitecture;
