// Logisim project homework_01.circ as structural Verilog
module main (
  input  a,
  input  b,
  input  c,
  input  d,
  output out_1,
  output out_2
);

  logic4 logic4_1 (.a(a), .b(b), .c(c), .d(d), .out1(out_1), .out2(out_2));
endmodule

// VHDL entity logic4, as the project stores it:
library ieee;
use ieee.std_logic_1164.all;

entity logic4 is
    port (
        a    : in  std_logic;
        b    : in  std_logic;
        c    : in  std_logic;
        d    : in  std_logic;
        out1 : out std_logic;
        out2 : out std_logic
    );
end entity logic4;

architecture behavioral of logic4 is
begin
    out1 <= a and b and c and d;
    out2 <= a or b or c or d;
end architecture behavioral;
