// Logisim project homework_04.circ as structural Verilog
module main (
  input  [24:0] vt,
  output result
);

  vote25 vote25_1 (.vt(vt), .result(result));
endmodule

// VHDL entity vote25, as the project stores it:
library ieee;
use ieee.std_logic_1164.all;

entity vote25 is
    port (
        vt     : in  std_logic_vector(24 downto 0);
        result : out std_logic
    );
end entity vote25;

architecture behavioral of vote25 is
begin
    process(vt)
        variable count : integer range 0 to 25;
    begin
        count := 0;
        for i in vt'range loop
            if vt(i) = '1' then
                count := count + 1;
            end if;
        end loop;

        if count >= 13 then
            result <= '1';
        else
            result <= '0';
        end if;
    end process;
end architecture behavioral;
