// Logisim project homework_all.circ as structural Verilog
module task1_logic4 (
  input  a,
  input  b,
  input  c,
  input  d,
  output out_1,
  output out_2
);

  logic4 logic4_1 (.a(a), .b(b), .c(c), .d(d), .out1(out_1), .out2(out_2));
endmodule

module task2_mux8 (
  input  a,
  input  b,
  input  c,
  input  d,
  input  e,
  input  f,
  input  g,
  input  h,
  input  [2:0] sel,
  output y
);

  mux8 mux8_1 (.a(a), .b(b), .c(c), .d(d), .e(e), .f(f), .g(g), .h(h), .sel(sel), .y(y));
endmodule

module task3_letters (
  input  [2:0] sel
);

  wire seg_a, seg_b, seg_c, seg_d, seg_dp, seg_e, seg_f, seg_g;

  letters7seg letters7seg_1 (
    .sel(sel), .a(seg_a), .b(seg_b), .c(seg_c), .d(seg_d), .e(seg_e), .f(seg_f), .g(seg_g), .dp(seg_dp));
  _7_Segment_Display u_7_segment_display_1 (
    .g(seg_g), .f(seg_f), .a(seg_a), .b(seg_b), .e(seg_e), .d(seg_d), .c(seg_c), .dp(seg_dp));
endmodule

module task4_vote25 (
  input  [24:0] vt,
  output result
);

  vote25 vote25_1 (.vt(vt), .result(result));
endmodule

module task5_popcount15 (
  input  [14:0] vt,
  input  en
);

  wire seg_a, seg_b, seg_c, seg_d, seg_dp, seg_e, seg_f, seg_g;

  popcount15 popcount15_1 (
    .vt(vt), .en(en), .a(seg_a), .b(seg_b), .c(seg_c), .d(seg_d), .e(seg_e), .f(seg_f), .g(seg_g), .dp(seg_dp));
  _7_Segment_Display u_7_segment_display_1 (
    .g(seg_g), .f(seg_f), .a(seg_a), .b(seg_b), .e(seg_e), .d(seg_d), .c(seg_c), .dp(seg_dp));
endmodule

// VHDL entity logic4, as the project stores it:
library ieee;
use ieee.std_logic_1164.all;

entity logic4 is
    port (
        a    : in  std_logic;
        b    : in  std_logic;
        c    : in  std_logic;
        d    : in  std_logic;
        out1 : out std_logic;
        out2 : out std_logic
    );
end entity logic4;

architecture behavioral of logic4 is
begin
    out1 <= a and b and c and d;
    out2 <= a or b or c or d;
end architecture behavioral;

// VHDL entity mux8, as the project stores it:
library ieee;
use ieee.std_logic_1164.all;

entity mux8 is
    port (
        a, b, c, d, e, f, g, h : in  std_logic;
        sel                     : in  std_logic_vector(2 downto 0);
        y                       : out std_logic
    );
end entity mux8;

architecture behavioral of mux8 is
begin
    with sel select
        y <= a   when "000",
             b   when "001",
             c   when "010",
             d   when "011",
             e   when "100",
             f   when "101",
             g   when "110",
             h   when "111",
             '0' when others;
end architecture behavioral;

// VHDL entity letters7seg, as the project stores it:
library ieee;
use ieee.std_logic_1164.all;

entity letters7seg is
    port (
        sel                 : in  std_logic_vector(2 downto 0);
        a, b, c, d, e, f, g : out std_logic;
        dp                  : out std_logic
    );
end entity letters7seg;

architecture behavioral of letters7seg is
    signal segments : std_logic_vector(6 downto 0);
begin
    with sel select
        segments <= "1111101" when "000",
                    "0011111" when "001",
                    "0001101" when "010",
                    "0111101" when "011",
                    "1000111" when "100",
                    "1111011" when "101",
                    "0000000" when others;

    a <= segments(6);
    b <= segments(5);
    c <= segments(4);
    d <= segments(3);
    e <= segments(2);
    f <= segments(1);
    g <= segments(0);
    dp <= '0';
end architecture behavioral;

// VHDL entity vote25, as the project stores it:
library ieee;
use ieee.std_logic_1164.all;

entity vote25 is
    port (
        vt     : in  std_logic_vector(24 downto 0);
        result : out std_logic
    );
end entity vote25;

architecture behavioral of vote25 is
begin
    process(vt)
        variable count : integer range 0 to 25;
    begin
        count := 0;
        for i in vt'range loop
            if vt(i) = '1' then
                count := count + 1;
            end if;
        end loop;

        if count >= 13 then
            result <= '1';
        else
            result <= '0';
        end if;
    end process;
end architecture behavioral;

// VHDL entity popcount15, as the project stores it:
library ieee;
use ieee.std_logic_1164.all;

entity popcount15 is
    port (
        vt                  : in  std_logic_vector(14 downto 0);
        en                  : in  std_logic;
        a, b, c, d, e, f, g : out std_logic;
        dp                  : out std_logic
    );
end entity popcount15;

architecture behavioral of popcount15 is
    signal segments : std_logic_vector(6 downto 0);
begin
    process(vt, en)
        variable count : integer range 0 to 15;
    begin
        count := 0;
        for i in vt'range loop
            if vt(i) = '1' then
                count := count + 1;
            end if;
        end loop;

        if en = '1' then
            case count is
                when 0      => segments <= "1111110";
                when 1      => segments <= "0110000";
                when 2      => segments <= "1101101";
                when 3      => segments <= "1111001";
                when 4      => segments <= "0110011";
                when 5      => segments <= "1011011";
                when 6      => segments <= "1011111";
                when 7      => segments <= "1110000";
                when 8      => segments <= "1111111";
                when 9      => segments <= "1111011";
                when 10     => segments <= "1110111";
                when 11     => segments <= "0011111";
                when 12     => segments <= "1001110";
                when 13     => segments <= "0111101";
                when 14     => segments <= "1001111";
                when 15     => segments <= "1000111";
                when others => segments <= "0000000";
            end case;
        else
            segments <= "0000000";
        end if;
    end process;

    a <= segments(6);
    b <= segments(5);
    c <= segments(4);
    d <= segments(3);
    e <= segments(2);
    f <= segments(1);
    g <= segments(0);
    dp <= '0';
end architecture behavioral;
